# Fritzing sketch P4 - Sensor_DHT11 (saved by Fritzing 0.9.3b)
breadboards: 1

parts:
  R1 = Resistor [tolerance=±5% resistance=330 package=THT]
  LED1 = LED - 5mm [color="Yellow (595nm)" package="5 mm [THT]"]
  R2 = Resistor [tolerance=±5% resistance=330 package=THT]
  LED2 = LED - 5mm [color="Yellow (595nm)" package="5 mm [THT]"]
  R3 = Resistor [tolerance=±5% resistance=330 package=THT]
  R4 = Resistor [tolerance=±5% resistance=330 package=THT]
  LED3 = LED - 5mm [color="Green (570nm)" package="5 mm [THT]"]
  LED4 = LED - 5mm [color="Green (570nm)" package="5 mm [THT]"]
  R5 = Resistor [tolerance=±5% resistance=330 package=THT]
  LED5 = LED - 5mm [color="Red (633nm)" package="5 mm [THT]"]
  R6 = Resistor [tolerance=±5% resistance=330 package=THT]
  LED6 = LED - 5mm [color="Red (633nm)" package="5 mm [THT]"]
  U1 = ESP32-38PinWide [part_number=ESP32-38PinWide]
  DHT1 = DHT11 Humitidy and Temperature Sensor

nets:
  N1: R1.Pin_0, LED1.anode
  N2: R1.Pin_1, U1.GPIO14
  GND: LED1.cathode, LED2.cathode, LED3.cathode, LED4.cathode, LED5.cathode, LED6.cathode, U1.GND, DHT1.GND
  N3: R2.Pin_0, LED2.anode
  N4: R2.Pin_1, U1.GPIO27
  N5: R3.Pin_0, LED3.anode
  N6: R3.Pin_1, U1.GPIO26
  N7: R4.Pin_0, LED4.anode
  N8: R4.Pin_1, U1.GPIO25
  N9: R5.Pin_0, LED5.anode
  N10: R5.Pin_1, U1.GPIO12
  N11: R6.Pin_0, LED6.anode
  N12: R6.Pin_1, U1.GPIO13
  N13: U1.3.3, DHT1.VDD
  N14: U1.GPIO33, DHT1.DATA

custom parts:
  ESP32-38PinWide: Generic 38-Pin ESP32 with wide format (only access to one side of pins on a breadboard) based on Stephen Lilley's HiLetgo ESP-WROOM-32 ESP32 ESP-32S Development Board.
  DHT11 Humitidy and Temperature Sensor: DHT11 Humidity and Temperature Sensor
